# Fritzing sketch gibbon-v1128 (saved by Fritzing 0.9.2b)
breadboards: 1

parts:
  mega = Arduino Mega 2560 (Rev3)
  IC1 = H-Bridge [package=THT]
  IC2 = H-Bridge [package=THT]
  IC3 = H-Bridge [package=THT]
  Fan1 = DC Motor  # not connected
  Fan2 = DC Motor  # not connected
  Fan3 = DC Motor  # not connected
  Fan4 = DC Motor  # not connected
  Fan5 = DC Motor  # not connected
  Fan6 = DC Motor  # not connected
  Bubble1 = Basic Servo  # not connected
  Bubble2 = Basic Servo  # not connected
  Bubble3 = Basic Servo  # not connected
  Bubble4 = Basic Servo  # not connected
  Bubble5 = Basic Servo  # not connected
  Bubble6 = Basic Servo  # not connected
  Servo2L = Basic Servo  # not connected
  Servo3R = Basic Servo  # not connected
  Servo3L = Basic Servo  # not connected
  Servo2R = Basic Servo  # not connected
  Servo1L = Basic Servo  # not connected
  Servo1R = Basic Servo  # not connected
  Servo5L = Basic Servo  # not connected
  Servo6R = Basic Servo  # not connected
  Servo6L = Basic Servo  # not connected
  Servo5R = Basic Servo  # not connected
  Servo4L = Basic Servo  # not connected
  Servo4R = Basic Servo  # not connected

nets:
  N1: mega.D19/RX1, IC3.4A
  N2: mega.D18/TX1, IC3.1A
  N3: mega.D17_PWM/RX2, IC2.4A
  N4: mega.D16_PWM/TX2, IC2.1A
  N5: mega.D15/RX3, IC1.4A
  N6: mega.D14/TX3, IC1.1A
  GND1: mega.GND, IC1.GND1, IC1.GND2, IC1.2A, IC1.3A, IC1.GND3, IC1.GND4, IC2.GND1, IC2.GND2, IC2.2A, IC2.3A, IC2.GND3, IC2.GND4, IC3.GND1, IC3.GND2, IC3.2A, IC3.3A, IC3.GND3, IC3.GND4
  N7: mega.5V, IC1.1_2EN, IC1.3_4EN, IC1.VCC1, IC2.1_2EN, IC2.3_4EN, IC2.VCC1, IC3.1_2EN, IC3.3_4EN, IC3.VCC1

notes:
  DCmotor(fan)
  1 +
  2 -
  3
  4
  5
  5
  6
  7
  8
  9
  10
  11
  12s
